// Logisim project arc.circ as structural Verilog: 7 circuits, main circuit main
module main (
  output [23:0] out_1,
  output [23:0] out_2,
  output [23:0] out_3,
  output [23:0] out_4,
  output [23:0] out_5,
  output [23:0] out_6,
  output [23:0] out_7,
  output [23:0] out_8
);

  wire CLK, ExtOp, MemRead, MemToReg, MemWrite, regW, Sf, undriven, undriven_2, undriven_3, undriven_4;
  wire [0:0] alu_1_zero_flag;
  wire [1:0] aluOP, AluSrc, cond, PCsrc, RcSlc, RegDst;
  wire [2:0] multiplexer_2_out, multiplexer_3_out, rd, rs, rt;
  wire [4:0] op;
  wire [7:0] StateReg;
  wire [9:0] imm10;
  wire [16:0] imm17;
  wire [23:0] adder_2_out, adder_3_out, alu_1_out, bit_extender_1_out, bit_extender_2_out, busB,
       extender_1_extendedout, extender_2_extendedout, multiplexer_1_out, multiplexer_4_out,
       multiplexer_5_out, PC, PC_q, ram_1_data, reg_1_bus_a, rom_1_data, shifter_1_out;

  Register #(.width(24)) u_PC (.D(multiplexer_1_out), .Q(PC_q), .clk(CLK));  // open: en, clr
  Clock clock_1 (.out(CLK));
  Adder #(.width(24)) adder_1 (.a(24'h1), .b(PC_q), .out(PC));  // open: cin, cout
  Multiplexer #(.select(2), .width(24)) multiplexer_1 (
    .in0(PC), .in1(adder_2_out), .in2(adder_3_out), .in3(reg_1_bus_a), .out(multiplexer_1_out), .sel(PCsrc));  // open: en
  ROM #(.addrWidth(24), .dataWidth(24)) rom_1 (.addr(PC_q), .data(rom_1_data));  // open: sel
  assign bit_extender_1_out = {{7{1'b0}}, imm17};  // Bit_Extender bit_extender_1
  decode decode_1 (
    .in_1(rom_1_data), .cond(cond), .op(op), .SF(Sf), .Rd(rd), .RS(rs), .Rt(rt), .Imm10(imm10), .Imm17(imm17));
  Adder #(.width(24)) adder_2 (.a(PC_q), .b(bit_extender_1_out), .out(adder_2_out));  // open: cin, cout
  Control_unit control_unit_1 (
    .OP(op), .cond(cond), .RsSlc(RcSlc), .zero(StateReg[0]), .ExtOp(ExtOp), .RegW(regW), .MemR(MemRead),
    .MemW(MemWrite), .MemReg(MemToReg), .RegDst(RegDst), .AluSrc(AluSrc), .AluOp(aluOP), .PcSrc(PCsrc));
  extender extender_1 (.Input(imm10), .ExtenderOP(ExtOp), .ExtendedOut(extender_1_extendedout));
  Multiplexer #(.width(3), .enable("false")) multiplexer_2 (
    .in0(rt), .in1(rd), .out(multiplexer_2_out), .sel(MemWrite));
  Multiplexer #(.select(2), .width(3)) multiplexer_3 (
    .in0(rd), .in1(rd), .in2(3'b111), .in3(3'b001), .out(multiplexer_3_out), .sel(RegDst));  // open: en
  Adder #(.width(24)) adder_3 (.a(PC_q), .b(extender_1_extendedout), .out(adder_3_out));  // open: cin, cout
  Reg reg_1 (
    .RA(rs), .CLK(CLK), .Bus_A(reg_1_bus_a), .Bus_B(busB), .R1(out_2), .R2(out_3), .R3(out_4), .R4(out_5),
    .R5(out_6), .R6(out_7), .R7(out_8), .Bus_Write(out_1), .RW(multiplexer_3_out), .Register_Write(regW),
    .RB(multiplexer_2_out));
  extender extender_2 (.Input(imm10), .ExtenderOP(ExtOp), .ExtendedOut(extender_2_extendedout));
  Multiplexer #(.select(2), .width(24)) multiplexer_4 (
    .in0(reg_1_bus_a), .in1(PC), .in2(shifter_1_out), .out(multiplexer_4_out), .sel(RcSlc));  // open: in3, en
  Multiplexer #(.select(2), .width(24)) multiplexer_5 (
    .in0(busB), .in1(extender_2_extendedout), .in2(24'h1), .in3({24{1'b0}}), .out(multiplexer_5_out),
    .sel(AluSrc));  // open: en
  assign bit_extender_2_out = {{7{1'b0}}, imm17};  // Bit_Extender bit_extender_2
  ALU alu_1 (
    .Opcode(aluOP), .in_1(multiplexer_4_out), .in_2(multiplexer_5_out), .Zero_Flag(alu_1_zero_flag[0]),
    .OUT(alu_1_out));
  Shifter #(.width(24)) shifter_1 (.in(bit_extender_2_out), .\dist (5'b00110), .out(shifter_1_out));
  RAM #(.addrWidth(24), .dataWidth(24), .bus("separate")) ram_1 (
    .addr(alu_1_out), .din(busB), .data(ram_1_data), .str(MemWrite), .clk(CLK), .ld(MemRead));  // open: sel, clr
  Multiplexer #(.width(24), .enable("false")) multiplexer_6 (
    .in0(alu_1_out), .in1(ram_1_data), .out(out_1), .sel(MemToReg));
  Register register_1 (.D({{7{1'b0}}, alu_1_zero_flag[0]}), .Q(StateReg));  // open: en, clk, clr
  RAM #(.addrWidth(16), .dataWidth(16), .bus("separate")) ram_2 ();  // open: addr, din, data, str, sel, clk, ld, clr
  RAM #(.addrWidth(16), .dataWidth(16), .bus("separate")) ram_3 ();  // open: addr, din, data, str, sel, clk, ld, clr
  RAM #(.addrWidth(16), .dataWidth(16), .bus("separate")) ram_4 ();  // open: addr, din, data, str, sel, clk, ld, clr
  RAM #(.addrWidth(16), .dataWidth(16), .bus("separate")) ram_5 (
    .sel(undriven), .clk(undriven_2), .ld(undriven_3), .clr(undriven_4));  // open: addr, din, data, str
  RAM #(.addrWidth(16), .dataWidth(16), .bus("separate")) ram_6 (
    .str(undriven), .sel(undriven_2), .clk(undriven_3), .ld(undriven_4));  // open: addr, din, data, clr

  // Other names for the same wires on the sheet: memOUT[23:0] = out_1; R1[23:0] = out_2; R2[23:0] = out_3;
  //   R3[23:0] = out_4; R4[23:0] = out_5; R5[23:0] = out_6; R6[23:0] = out_7; R7[23:0] = out_8; Zero = StateReg[0]

  // Notes on the sheet:
  //   contents of rom_1 (hex, n*v repeats v):
  //   0 10280a 104c04 86880 58000f 14400a 12800a 9c0001 c0000
  //   RA
  //   RB
  //   rw
  //   regW
  //   clk
  //   busW
  //   busA
  //   busB
endmodule

// Register file
module Reg (
  input  [23:0] Bus_Write,
  input  Register_Write,
  input  [2:0] RA,
  input  [2:0] RW,
  input  CLK,
  input  [2:0] RB,
  output [23:0] R1,
  output [23:0] R2,
  output [23:0] Bus_A,
  output [23:0] R3,
  output [23:0] R4,
  output [23:0] R5,
  output [23:0] R6,
  output [23:0] Bus_B,
  output [23:0] R7
);

  wire and_1_out, and_2_out, and_3_out, and_4_out, and_5_out, and_6_out, and_7_out, and_8_out,
       decoder_1_out0, decoder_1_out1, decoder_1_out2, decoder_1_out3, decoder_1_out4, decoder_1_out5,
       decoder_1_out6, decoder_1_out7;
  wire [23:0] Reg0;

  Decoder #(.select(3), .enable("false")) decoder_1 (
    .out0(decoder_1_out0), .out1(decoder_1_out1), .out2(decoder_1_out2), .out3(decoder_1_out3),
    .out4(decoder_1_out4), .out5(decoder_1_out5), .out6(decoder_1_out6), .out7(decoder_1_out7), .sel(RW));
  and and_1 (and_1_out, Register_Write, decoder_1_out0);
  and and_2 (and_2_out, Register_Write, decoder_1_out1);
  and and_3 (and_3_out, Register_Write, decoder_1_out2);
  and and_4 (and_4_out, Register_Write, decoder_1_out3);
  and and_5 (and_5_out, Register_Write, decoder_1_out4);
  and and_6 (and_6_out, Register_Write, decoder_1_out5);
  and and_7 (and_7_out, Register_Write, decoder_1_out6);
  and and_8 (and_8_out, Register_Write, decoder_1_out7);
  Register #(.width(24), .trigger("falling")) register_1 (
    .D({24{1'b0}}), .en(and_1_out), .Q(Reg0), .clk(CLK));  // open: clr
  Register #(.width(24), .trigger("falling")) register_2 (
    .D(Bus_Write), .en(and_2_out), .Q(R1), .clk(CLK));  // open: clr
  Register #(.width(24), .trigger("falling")) register_3 (
    .D(Bus_Write), .en(and_3_out), .Q(R2), .clk(CLK));  // open: clr
  Register #(.width(24), .trigger("falling")) register_4 (
    .D(Bus_Write), .en(and_4_out), .Q(R3), .clk(CLK));  // open: clr
  Register #(.width(24), .trigger("falling")) register_5 (
    .D(Bus_Write), .en(and_5_out), .Q(R4), .clk(CLK));  // open: clr
  Register #(.width(24), .trigger("falling")) register_6 (
    .D(Bus_Write), .en(and_6_out), .Q(R5), .clk(CLK));  // open: clr
  Register #(.width(24), .trigger("falling")) register_7 (
    .D(Bus_Write), .en(and_7_out), .Q(R6), .clk(CLK));  // open: clr
  Register #(.width(24), .trigger("falling")) register_8 (
    .D(Bus_Write), .en(and_8_out), .Q(R7), .clk(CLK));  // open: clr
  Multiplexer #(.select(3), .width(24), .enable("false")) multiplexer_1 (
    .in0(Reg0), .in1(R1), .in2(R2), .in3(R3), .in4(R4), .in5(R5), .in6(R6), .in7(R7), .out(Bus_A), .sel(RA));
  Multiplexer #(.select(3), .width(24), .enable("false")) multiplexer_2 (
    .in0(Reg0), .in1(R1), .in2(R2), .in3(R3), .in4(R4), .in5(R5), .in6(R6), .in7(R7), .out(Bus_B), .sel(RB));

  // Other names for the same wires on the sheet: Reg1[23:0] = R1; Reg2[23:0] = R2; Reg3[23:0] = R3; Reg4[23:0] = R4;
  //   Reg5[23:0] = R5; Reg6[23:0] = R6; Reg7[23:0] = R7
endmodule

module ALU (
  input  [23:0] in_1,
  input  [23:0] in_2,
  input  [1:0] Opcode,
  output [23:0] OUT,
  output Zero_Flag
);

  wire comparator_1_gt;
  wire [23:0] ADD_R, AND, cas, SUB_r;

  Comparator #(.width(24)) comparator_1 (.a(in_1), .b(in_2), .gt(comparator_1_gt), .eq(Zero_Flag));  // open: lt
  Adder #(.width(24)) adder_1 (.a(in_2), .b(in_1), .out(ADD_R));  // open: cin, cout
  Subtractor #(.width(24)) subtractor_1 (.a(in_2), .b(in_1), .out(SUB_r));  // open: bin, bout
  Multiplexer #(.width(24)) multiplexer_1 (.in0(in_1), .in1(in_2), .out(cas), .sel(comparator_1_gt));  // open: en
  assign AND = in_1 & in_2;  // AND_Gate and_1, 24 bits wide
  Multiplexer #(.select(2), .width(24), .enable("false")) multiplexer_2 (
    .in0(AND), .in1(cas), .in2(ADD_R), .in3(SUB_r), .out(OUT), .sel(Opcode));

  // Notes on the sheet:
  //   Rs
  //   Rt
endmodule

module decode (
  input  [23:0] in_1,
  output [1:0] cond,
  output [4:0] op,
  output SF,
  output [2:0] Rd,
  output [2:0] RS,
  output [2:0] Rt,
  output [9:0] Imm10,
  output [16:0] Imm17
);


  assign cond = in_1[23:22];
  assign Imm10 = in_1[9:0];
  assign Imm17 = in_1[16:0];
  assign op = in_1[21:17];
  assign Rd = in_1[15:13];
  assign RS = in_1[12:10];
  assign Rt = in_1[9:7];
  assign SF = in_1[16];
endmodule

module extender (
  input  ExtenderOP,
  input  [9:0] Input,
  output [23:0] ExtendedOut
);

  and and_1 (ExtendedOut[23], ExtenderOP, Input[9]);

  assign ExtendedOut[22:0] = {{13{ExtendedOut[23]}}, Input};
endmodule

module Control_unit (
  input  [4:0] OP,
  input  zero,
  input  [1:0] cond,
  output [1:0] RsSlc,
  output RegW,
  output [1:0] AluSrc,
  output [1:0] RegDst,
  output [1:0] PcSrc,
  output ExtOp,
  output MemR,
  output [1:0] AluOp,
  output MemW,
  output MemReg
);

  wire ADD, ADDI, AND, and_1_out, and_2_out, and_3_out, ANDI, BEQ, CAS, CMP, enable, eq, inv_out, J, JR, LW,
       LWS, neq, nop, normal, or_4_out, or_5_out, or_8_out, or_10_out, SUB, SW;

  Decoder #(.select(2)) decoder_1 (.out0(normal), .out1(eq), .out2(neq), .out3(nop), .sel(cond));  // open: en
  Decoder #(.select(5)) decoder_2 (
    .out0(AND), .out1(CAS), .out2(LWS), .out3(ADD), .out4(SUB), .out5(CMP), .out6(JR), .out7(ANDI),
    .out8(ADDI), .out9(LW), .out10(SW), .out11(BEQ), .out12(J), .out13(RsSlc[0]), .out14(RsSlc[1]), .sel(OP));  // open: out15, out16, out17, out18, out19, out20, out21, out22, out23, out24, out25, out26, out27, out28, out29, out30, out31, en
  and and_1 (and_1_out, eq, zero);
  and and_2 (and_2_out, neq, inv_out);
  not inv (inv_out, zero);
  or or_1 (enable, and_1_out, normal, and_2_out);
  and and_3 (and_3_out, BEQ, zero);
  or or_2 (AluSrc[0], ADDI, ANDI, SW, LW, RsSlc[1]);
  or or_3 (AluSrc[1], RsSlc[0], RsSlc[1]);
  or or_4 (or_4_out, J, RsSlc[0], JR);
  or or_5 (or_5_out, and_3_out, JR);
  and and_4 (PcSrc[0], enable, or_4_out);
  and and_5 (PcSrc[1], or_5_out, enable);
  or or_6 (AluOp[0], AND, CAS, SUB, ANDI);
  or or_7 (AluOp[1], SW, LW, ADDI, LWS, ADD, SUB, RsSlc[0], RsSlc[1]);
  or or_8 (or_8_out, AND, CAS, LWS, ADD, SUB, ANDI, ADDI, LW, RsSlc[0], RsSlc[1]);
  or or_9 (ExtOp, ADDI, LW, SW, BEQ);
  or or_10 (or_10_out, LW, LWS);
  or or_11 (MemReg, LW, LWS);
  and and_6 (RegW, or_8_out, enable);
  and and_7 (MemR, or_10_out, enable);
  and and_8 (MemW, SW, enable);

  assign RegDst = AluSrc;

  // Other names for the same wires on the sheet: JAL_prime = RsSlc[0]; LUI = RsSlc[1]
endmodule

module HazardForward (
  input  MEM_WB_RegisterWrite,
  input  EX_MEM_RegisterWrite,
  input  [2:0] Mem_RD,
  input  [2:0] ID_EX_RS,
  input  [2:0] MEM_WB_RD,
  input  [2:0] ID_EX_RT,
  input  [2:0] IF_ID_RS,
  input  [2:0] IF_ID_RT,
  input  ID_EX_MEMRead,
  output [1:0] Forward_A,
  output [1:0] Forward_B,
  output Stall
);

  wire comparator_1_eq, comparator_2_eq, comparator_3_eq, comparator_4_eq, comparator_5_eq, comparator_6_eq,
       comparator_7_eq, comparator_8_eq, comparator_9_eq, not_1_out, not_2_out, not_3_out, not_4_out,
       or_1_out, undriven_3, undriven_4, undriven_5, undriven_10;
  wire [1:0] multiplexer_1_out, multiplexer_2_out, undriven_6, undriven_7, undriven_8, undriven_9;
  wire [2:0] undriven, undriven_2;

  Comparator #(.width(3)) comparator_1 (.a(undriven_2), .b(IF_ID_RS), .eq(comparator_1_eq));  // open: gt, lt
  Comparator #(.width(3)) comparator_2 (.a(undriven_2), .b(undriven), .eq(comparator_2_eq));  // open: gt, lt
  Comparator #(.width(3)) comparator_3 (.a(Mem_RD), .b(3'b000), .eq(comparator_3_eq));  // open: gt, lt
  Comparator #(.width(3)) comparator_4 (.a(Mem_RD), .b(ID_EX_RS), .eq(comparator_4_eq));  // open: gt, lt
  Comparator #(.width(3)) comparator_5 (.a(MEM_WB_RD), .b(3'b000), .eq(comparator_5_eq));  // open: gt, lt
  Comparator #(.width(3)) comparator_6 (.a(Mem_RD), .b(ID_EX_RS), .eq(comparator_6_eq));  // open: gt, lt
  Comparator #(.width(3)) comparator_7 (.a(MEM_WB_RD), .b(ID_EX_RS), .eq(comparator_7_eq));  // open: gt, lt
  Comparator #(.width(3)) comparator_8 (.a(Mem_RD), .b(3'b000), .eq(comparator_8_eq));  // open: gt, lt
  Comparator #(.width(3)) comparator_9 (.a(Mem_RD), .b(ID_EX_RT), .eq(comparator_9_eq));  // open: gt, lt
  not not_1 (not_1_out, comparator_3_eq);
  not not_2 (not_2_out, comparator_5_eq);
  not not_3 (not_3_out, comparator_6_eq);
  not not_4 (not_4_out, comparator_8_eq);
  or or_1 (or_1_out, comparator_1_eq, comparator_2_eq);
  and and_1 (Stall, ID_EX_MEMRead, or_1_out);
  Multiplexer #(.width(2), .enable("false")) multiplexer_1 (
    .in0(undriven_6), .in1(undriven_7), .out(multiplexer_1_out), .sel(undriven_3));
  Multiplexer #(.width(2), .enable("false")) multiplexer_2 (
    .in0(undriven_8), .in1(undriven_9), .out(multiplexer_2_out), .sel(undriven_10));
  Multiplexer #(.width(2), .enable("false")) multiplexer_3 (
    .in0(multiplexer_1_out), .in1(2'b01), .out(Forward_A), .sel(undriven_4));
  Multiplexer #(.width(2), .enable("false")) multiplexer_4 (
    .in0(multiplexer_2_out), .in1(2'b01), .out(Forward_B), .sel(undriven_5));

  // Notes on the sheet:
  //   10
endmodule
